# Fritzing sketch insect-bot-power (saved by Fritzing 0.7.0b)
breadboards: 1

parts:
  S1 = Toggle Switch [package=THT]
  D1 = Rectifier Diode [part_number=1N4001 package="300 mil [THT]"]
  U1 = Voltage Regulator - 5V [package="TO220 [THT]"]
  C2 = Electrolytic Capacitor [capacitance=10µF package="100 mil [THT, electrolytic]"]
  C3 = Ceramic Capacitor [capacitance=100nF package="100 mil [THT, multilayer]"]
  R1 = Resistor [tolerance=±5% resistance=330 package=THT]
  U2 = mystery part, 2 pins [chip_label="PTC 500 mA" spacing=300mil]
  J1 = male pin header, 2 pins [form="♂ (male)"]
  J2 = male pin header, 2 pins [form="♂ (male)"]
  LED1 = LED - 3mm [color="Green (570nm)" package="3 mm [THT]"]
  C1 = Electrolytic Capacitor [capacitance=0.1mF package="100 mil [THT, electrolytic]"]

nets:
  N1: S1.COM, J1.pin2
  N2: S1.L2, D1.anode
  N3: D1.cathode, U2.pin1
  N4: U1.input_voltage, U2.pin2, C1.+
  N5: U1.GND, C2.-, C3.0, J1.pin1, J2.pin2, LED1.anode, C1.-
  N6: U1.output_voltage, C2.+, C3.1, R1.Pin_0, J2.pin1
  N7: R1.Pin_1, LED1.cathode
